# Fritzing sketch BNO055 (saved by Fritzing 0.9.3b)
circuit board: 10cm x 6cm

parts:
  Componente2 = Arduino Nano (Rev3.0)
  R1 = Basic Flex Resistor
  R2 = Resistor [tolerance=±5% resistance=10k package=THT]
  Componente3 = 9-DOF Absolute Orientation IMU Fusion Breakout - BNO055

nets:
  GND: Componente2.GND, R1.pin_1, Componente3.GND
  N1: Componente2.VIN, R2.Pin_0, Componente3.5.0V
  N2: Componente2.A5, Componente3.SCL_5V
  N3: Componente2.A4, Componente3.SDA_5V
  N4: Componente2.A0, R1.Pin_2, R2.Pin_1

notes:
  [BNO055
  x5 Flexores
  x2 sets

custom parts:
  9-DOF Absolute Orientation IMU Fusion Breakout - BNO055: A MEMS accelerometer, magnetometer and gyroscope on a single die with a high speed ARM Cortex-M0 based processor to digest all the sensor data, abstract the sensor fusion and real time requirements away, and spit out data you can use in quaternions, Euler angles or vectors.
